// Logisim project Rams.circ as structural Verilog
module main (
  input  [1:0] in_1,
  input  in_2,
  input  [15:0] FORCE_WRITE,
  input  in_4,
  input  [2:0] A_REG,
  input  [2:0] B_REG,
  input  [2:0] WRITE_REG,
  input  WRITE_DATA,
  input  CLK,
  output [15:0] out_10
);

  wire alu_16_bits_1_overflow, alu_16_bits_1_zero;
  wire [15:0] registerfile_1_out_a, registerfile_1_out_b;

  RegisterFile registerfile_1 (
    .DATA(out_10), .CLK(CLK), .OUT_A(registerfile_1_out_a), .OUT_B(registerfile_1_out_b),
    .WRITE_DATA(WRITE_DATA), .in_5(WRITE_REG), .REG_A(A_REG), .REG_B(B_REG));
  ALU_16_bits alu_16_bits_1 (
    .a(registerfile_1_out_a), .b(registerfile_1_out_b), .Operation(in_1), .Ainvert(in_2), .Bnegate(in_4),
    .Overflow(alu_16_bits_1_overflow), .Result(out_10), .Zero(alu_16_bits_1_zero));
  LED led_1 (.in(alu_16_bits_1_overflow));
  LED led_2 (.in(alu_16_bits_1_zero));
endmodule

// ALU
module ALU_1_bit (
  input  a,
  input  Ainvert,
  input  b,
  input  CarryIn,
  input  [1:0] Operation,
  input  Binvert,
  input  Less,
  output Set,
  output Result,
  output CarryOut
);

  wire and_1_out, multiplexer_1_out, multiplexer_2_out, not_1_out, not_2_out, or_1_out;

  not not_1 (not_1_out, a);
  not not_2 (not_2_out, b);
  Multiplexer multiplexer_1 (.in0(a), .in1(not_1_out), .out(multiplexer_1_out), .sel(Ainvert));  // open: en
  Multiplexer multiplexer_2 (.in0(b), .in1(not_2_out), .out(multiplexer_2_out), .sel(Binvert));  // open: en
  and and_1 (and_1_out, multiplexer_1_out, multiplexer_2_out);
  or or_1 (or_1_out, multiplexer_1_out, multiplexer_2_out);
  Adder #(.width(1)) adder_1 (.a(multiplexer_1_out), .b(multiplexer_2_out), .out(Set), .cin(CarryIn), .cout(CarryOut));
  Multiplexer #(.select(2)) multiplexer_3 (
    .in0(and_1_out), .in1(or_1_out), .in2(Set), .in3(Less), .out(Result), .sel(Operation));  // open: en
endmodule

module ALU_16_bits (
  input  Ainvert,
  input  Bnegate,
  input  [1:0] Operation,
  input  [15:0] a,
  input  [15:0] b,
  output [15:0] Result,
  output Zero,
  output Overflow
);

  wire alu_1_bit_1_carryout, alu_1_bit_2_carryout, alu_1_bit_3_carryout, alu_1_bit_4_carryout,
       alu_1_bit_5_carryout, alu_1_bit_6_carryout, alu_1_bit_7_carryout, alu_1_bit_8_carryout,
       alu_1_bit_9_carryout, alu_1_bit_10_carryout, alu_1_bit_11_carryout, alu_1_bit_12_carryout,
       alu_1_bit_13_carryout, alu_1_bit_14_carryout, alu_1_bit_15_carryout, alu_1_bit_16_set, or_1_out;

  ALU_1_bit alu_1_bit_1 (
    .a(a[0]), .b(b[0]), .Less(alu_1_bit_16_set), .Ainvert(Ainvert), .Result(Result[0]), .CarryIn(Bnegate),
    .Operation(Operation), .Binvert(Bnegate), .CarryOut(alu_1_bit_1_carryout));  // open: Set
  ALU_1_bit alu_1_bit_2 (
    .a(a[1]), .b(b[1]), .Less(1'b0), .Ainvert(Ainvert), .Result(Result[1]), .CarryIn(alu_1_bit_1_carryout),
    .Operation(Operation), .Binvert(Bnegate), .CarryOut(alu_1_bit_2_carryout));  // open: Set
  ALU_1_bit alu_1_bit_3 (
    .a(a[2]), .b(b[2]), .Less(1'b0), .Ainvert(Ainvert), .Result(Result[2]), .CarryIn(alu_1_bit_2_carryout),
    .Operation(Operation), .Binvert(Bnegate), .CarryOut(alu_1_bit_3_carryout));  // open: Set
  ALU_1_bit alu_1_bit_4 (
    .a(a[3]), .b(b[3]), .Less(1'b0), .Ainvert(Ainvert), .Result(Result[3]), .CarryIn(alu_1_bit_3_carryout),
    .Operation(Operation), .Binvert(Bnegate), .CarryOut(alu_1_bit_4_carryout));  // open: Set
  ALU_1_bit alu_1_bit_5 (
    .a(a[4]), .b(b[4]), .Less(1'b0), .Ainvert(Ainvert), .Result(Result[4]), .CarryIn(alu_1_bit_4_carryout),
    .Operation(Operation), .Binvert(Bnegate), .CarryOut(alu_1_bit_5_carryout));  // open: Set
  ALU_1_bit alu_1_bit_6 (
    .a(a[5]), .b(b[5]), .Less(1'b0), .Ainvert(Ainvert), .Result(Result[5]), .CarryIn(alu_1_bit_5_carryout),
    .Operation(Operation), .Binvert(Bnegate), .CarryOut(alu_1_bit_6_carryout));  // open: Set
  ALU_1_bit alu_1_bit_7 (
    .a(a[6]), .b(b[6]), .Less(1'b0), .Ainvert(Ainvert), .Result(Result[6]), .CarryIn(alu_1_bit_6_carryout),
    .Operation(Operation), .Binvert(Bnegate), .CarryOut(alu_1_bit_7_carryout));  // open: Set
  ALU_1_bit alu_1_bit_8 (
    .a(a[7]), .b(a[7]), .Less(1'b0), .Ainvert(Ainvert), .Result(Result[7]), .CarryIn(alu_1_bit_7_carryout),
    .Operation(Operation), .Binvert(Bnegate), .CarryOut(alu_1_bit_8_carryout));  // open: Set
  ALU_1_bit alu_1_bit_9 (
    .a(a[8]), .b(b[8]), .Less(1'b0), .Ainvert(Ainvert), .Result(Result[8]), .CarryIn(alu_1_bit_8_carryout),
    .Operation(Operation), .Binvert(Bnegate), .CarryOut(alu_1_bit_9_carryout));  // open: Set
  ALU_1_bit alu_1_bit_10 (
    .a(a[9]), .b(b[9]), .Less(1'b0), .Ainvert(Ainvert), .Result(Result[9]), .CarryIn(alu_1_bit_9_carryout),
    .Operation(Operation), .Binvert(Bnegate), .CarryOut(alu_1_bit_10_carryout));  // open: Set
  ALU_1_bit alu_1_bit_11 (
    .a(a[10]), .b(b[10]), .Less(1'b0), .Ainvert(Ainvert), .Result(Result[10]),
    .CarryIn(alu_1_bit_10_carryout), .Operation(Operation), .Binvert(Bnegate),
    .CarryOut(alu_1_bit_11_carryout));  // open: Set
  ALU_1_bit alu_1_bit_12 (
    .a(a[11]), .b(b[11]), .Less(1'b0), .Ainvert(Ainvert), .Result(Result[11]),
    .CarryIn(alu_1_bit_11_carryout), .Operation(Operation), .Binvert(Bnegate),
    .CarryOut(alu_1_bit_12_carryout));  // open: Set
  ALU_1_bit alu_1_bit_13 (
    .a(a[12]), .b(b[12]), .Less(1'b0), .Ainvert(Ainvert), .Result(Result[12]),
    .CarryIn(alu_1_bit_12_carryout), .Operation(Operation), .Binvert(Bnegate),
    .CarryOut(alu_1_bit_13_carryout));  // open: Set
  ALU_1_bit alu_1_bit_14 (
    .a(a[13]), .b(b[13]), .Less(1'b0), .Ainvert(Ainvert), .Result(Result[13]),
    .CarryIn(alu_1_bit_13_carryout), .Operation(Operation), .Binvert(Bnegate),
    .CarryOut(alu_1_bit_14_carryout));  // open: Set
  ALU_1_bit alu_1_bit_15 (
    .a(a[14]), .b(b[14]), .Less(1'b0), .Ainvert(Ainvert), .Result(Result[14]),
    .CarryIn(alu_1_bit_14_carryout), .Operation(Operation), .Binvert(Bnegate),
    .CarryOut(alu_1_bit_15_carryout));  // open: Set
  ALU_1_bit alu_1_bit_16 (
    .a(a[15]), .b(b[15]), .Less(1'b0), .Ainvert(Ainvert), .Result(Result[15]),
    .CarryIn(alu_1_bit_15_carryout), .Operation(Operation), .Binvert(Bnegate), .Set(alu_1_bit_16_set),
    .CarryOut(Overflow));
  or or_1 (or_1_out, Result[0], Result[1], Result[2], Result[3], Result[4], Result[5], Result[6], Result[7], Result[8], Result[9], Result[10], Result[11], Result[12], Result[13], Result[14], Result[15]);
  not not_1 (Zero, or_1_out);

  assign b[7] = a[7];
endmodule

module RegisterFile (
  input  [15:0] DATA,
  input  [2:0] REG_A,
  input  CLK,
  input  WRITE_DATA,
  input  [2:0] in_5,
  input  [2:0] REG_B,
  output [15:0] OUT_A,
  output [15:0] OUT_B
);

  wire demultiplexer_1_out1, demultiplexer_1_out2, demultiplexer_1_out3, demultiplexer_1_out4,
       demultiplexer_1_out5, demultiplexer_1_out7;
  wire [15:0] register_1_q, register_2_q, register_3_q, register_4_q, register_5_q, register_6_q,
       register_7_q, register_8_q;

  Demultiplexer #(.select(3)) demultiplexer_1 (
    .out1(demultiplexer_1_out1), .out2(demultiplexer_1_out2), .out3(demultiplexer_1_out3),
    .out4(demultiplexer_1_out4), .out5(demultiplexer_1_out5), .out6(demultiplexer_1_out5),
    .out7(demultiplexer_1_out7), .in(CLK), .sel(in_5), .en(WRITE_DATA));  // open: out0
  Register #(.width(16)) register_1 (.D(DATA), .Q(register_1_q));  // open: en, clk, clr
  Register #(.width(16)) register_2 (.D(DATA), .Q(register_2_q), .clk(demultiplexer_1_out1));  // open: en, clr
  Register #(.width(16)) register_3 (.D(DATA), .Q(register_3_q), .clk(demultiplexer_1_out2));  // open: en, clr
  Register #(.width(16)) register_4 (.D(DATA), .Q(register_4_q), .clk(demultiplexer_1_out3));  // open: en, clr
  Register #(.width(16)) register_5 (.D(DATA), .Q(register_5_q), .clk(demultiplexer_1_out4));  // open: en, clr
  Register #(.width(16)) register_6 (.D(DATA), .Q(register_6_q), .clk(demultiplexer_1_out5));  // open: en, clr
  Register #(.width(16)) register_7 (.D(DATA), .Q(register_7_q), .clk(demultiplexer_1_out5));  // open: en, clr
  Register #(.width(16)) register_8 (.D(DATA), .Q(register_8_q), .clk(demultiplexer_1_out7));  // open: en, clr
  Multiplexer #(.select(3), .width(16)) multiplexer_1 (
    .in0(register_1_q), .in1(register_2_q), .in2(register_3_q), .in3(register_4_q), .in4(register_5_q),
    .in5(register_6_q), .in6(register_7_q), .in7(register_8_q), .out(OUT_A), .sel(REG_A));  // open: en
  Multiplexer #(.select(3), .width(16)) multiplexer_2 (
    .in0(register_1_q), .in1(register_2_q), .in2(register_3_q), .in3(register_4_q), .in4(register_5_q),
    .in5(register_6_q), .in6(register_7_q), .in7(register_8_q), .out(OUT_B), .sel(REG_B));  // open: en
endmodule

module k (
  input  in_1,
  input  in_2,
  input  in_3,
  input  in_4,
  input  in_5,
  input  in_6,
  output RegDest,
  output Branch,
  output MemRead,
  output MemToReg,
  output ALUOp0,
  output ALUOp1,
  output MemWrite,
  output ALUSrc,
  output RegWrite
);
endmodule

module Control_alpha (
  input  a,
  input  b,
  input  c,
  input  d,
  input  e,
  input  f,
  output RegDest,
  output Branch,
  output MemRead,
  output MemToReg,
  output ALUOp0,
  output ALUOp1,
  output MemWrite,
  output ALUSrc,
  output RegWrite,
  output Jump
);

  wire and_2_out, and_3_out, and_4_out, and_5_out, and_6_out, and_7_out, and_8_out, and_9_out, and_10_out,
       and_11_out, and_12_out, and_13_out, and_14_out, and_15_out, and_16_out, and_17_out, and_18_out,
       and_19_out, and_20_out, and_21_out, and_22_out, and_23_out, and_24_out, not_1_out, not_2_out,
       not_3_out, not_4_out, not_5_out, not_6_out, not_7_out, not_8_out, not_9_out, not_10_out, not_11_out,
       not_12_out, not_13_out, not_14_out, not_15_out, not_16_out, not_17_out, not_18_out, not_19_out,
       not_20_out, not_21_out, not_22_out, not_23_out, not_24_out, not_25_out, not_26_out, not_27_out,
       not_28_out, not_29_out, not_30_out, not_31_out, not_32_out, not_33_out, not_34_out, not_35_out,
       not_36_out, not_37_out, not_38_out;

  not not_1 (not_1_out, d);
  not not_2 (not_2_out, e);
  not not_3 (not_3_out, f);
  not not_4 (not_4_out, c);
  not not_5 (not_5_out, e);
  not not_6 (not_6_out, f);
  not not_7 (not_7_out, c);
  not not_8 (not_8_out, d);
  not not_9 (not_9_out, e);
  not not_10 (not_10_out, c);
  not not_11 (not_11_out, e);
  not not_12 (not_12_out, f);
  not not_13 (not_13_out, c);
  not not_14 (not_14_out, d);
  not not_15 (not_15_out, e);
  not not_16 (not_16_out, e);
  not not_17 (not_17_out, c);
  not not_18 (not_18_out, d);
  not not_19 (not_19_out, f);
  not not_20 (not_20_out, c);
  not not_21 (not_21_out, e);
  not not_22 (not_22_out, c);
  not not_23 (not_23_out, d);
  not not_24 (not_24_out, d);
  not not_25 (not_25_out, e);
  not not_26 (not_26_out, c);
  not not_27 (not_27_out, d);
  not not_28 (not_28_out, f);
  not not_29 (not_29_out, e);
  not not_30 (not_30_out, f);
  not not_31 (not_31_out, d);
  not not_32 (not_32_out, c);
  not not_33 (not_33_out, f);
  not not_34 (not_34_out, c);
  not not_35 (not_35_out, e);
  not not_36 (not_36_out, d);
  and and_1 (Jump, c, e, f);
  not not_37 (not_37_out, c);
  not not_38 (not_38_out, e);
  and and_2 (and_2_out, not_1_out, f);
  and and_3 (and_3_out, c, not_2_out, not_3_out);
  and and_4 (and_4_out, c, d, e);
  and and_5 (and_5_out, not_4_out, not_5_out, not_6_out);
  and and_6 (and_6_out, not_7_out, e, f);
  and and_7 (and_7_out, c, not_8_out, not_9_out, f);
  and and_8 (and_8_out, not_10_out, not_11_out, not_12_out);
  and and_9 (and_9_out, not_13_out, e, f);
  and and_10 (and_10_out, c, not_14_out, not_15_out, f);
  and and_11 (and_11_out, c, e, f);
  and and_12 (and_12_out, c, d, not_16_out);
  and and_13 (and_13_out, not_17_out, not_18_out, not_19_out);
  and and_14 (and_14_out, not_20_out, d, not_21_out, f);
  and and_15 (and_15_out, not_22_out, not_23_out, f);
  and and_16 (and_16_out, not_24_out, not_25_out, f);
  and and_17 (and_17_out, not_26_out, d, e);
  and and_18 (and_18_out, c, not_27_out, e, not_28_out);
  and and_19 (and_19_out, c, d, not_29_out, not_30_out);
  and and_20 (and_20_out, not_31_out, f);
  and and_21 (and_21_out, not_32_out, d, not_33_out);
  and and_22 (and_22_out, not_34_out, d, e);
  and and_23 (and_23_out, c, not_35_out, f);
  and and_24 (and_24_out, c, not_36_out, e);
  or or_1 (RegDest, not_37_out, not_38_out, and_2_out);
  or or_2 (Branch, and_3_out, and_4_out);
  or or_3 (MemRead, and_5_out, and_6_out, and_7_out);
  or or_4 (MemToReg, and_8_out, and_9_out, and_10_out);
  or or_5 (ALUOp1, and_11_out, and_12_out);
  or or_6 (MemWrite, and_13_out, and_14_out);
  or or_7 (ALUSrc, and_15_out, and_16_out, and_17_out, and_18_out, and_19_out);
  or or_8 (RegWrite, and_20_out, and_21_out, and_22_out, and_23_out, and_24_out);

  assign ALUOp0 = 1'b1;
endmodule

module test (
  input  CLK,
  input  reset
);

  wire control_alpha_1_branch;
  wire [2:0] multiplexer_1_out;
  wire [15:0] adder_1_out, alu_16_bits_1_result, bit_extender_1_out, multiplexer_2_out, multiplexer_3_out,
       multiplexer_4_out, PC_q, ram_1_data, registerfile_1_out_a, registerfile_1_out_b, rom_1_data;

  Register #(.width(16)) PC (.D(multiplexer_3_out), .Q(PC_q), .clk(CLK), .clr(reset));  // open: en
  ROM #(.addrWidth(16), .dataWidth(16)) rom_1 (.addr(PC_q), .data(rom_1_data));  // open: sel
  Adder #(.width(16)) adder_1 (.a(16'h2), .b(PC_q), .out(adder_1_out));  // open: cin, cout
  Control_alpha control_alpha_1 (
    .a(rom_1_data[15]), .b(rom_1_data[14]), .c(rom_1_data[13]), .d(rom_1_data[12]), .e(rom_1_data[11]),
    .f(rom_1_data[10]), .Branch(control_alpha_1_branch));  // open: RegDest, MemRead, MemToReg, ALUOp0, ALUOp1, MemWrite, ALUSrc, RegWrite, Jump
  Multiplexer #(.width(3)) multiplexer_1 (
    .in0({rom_1_data[4], rom_1_data[5], rom_1_data[6]}), .in1({rom_1_data[1], rom_1_data[2], rom_1_data[3]}),
    .out(multiplexer_1_out));  // open: sel, en
  assign bit_extender_1_out = {{6{1'b0}}, rom_1_data[9:0]};  // Bit_Extender bit_extender_1
  RegisterFile registerfile_1 (
    .DATA(multiplexer_4_out), .OUT_A(registerfile_1_out_a), .OUT_B(registerfile_1_out_b),
    .in_5(multiplexer_1_out), .REG_A({rom_1_data[7], rom_1_data[8], rom_1_data[9]}),
    .REG_B({rom_1_data[4], rom_1_data[5], rom_1_data[6]}));  // open: CLK, WRITE_DATA
  Multiplexer #(.width(16)) multiplexer_2 (
    .in0(registerfile_1_out_b), .in1(bit_extender_1_out), .out(multiplexer_2_out));  // open: sel, en
  Multiplexer #(.width(16)) multiplexer_3 (
    .in0(adder_1_out), .in1(bit_extender_1_out), .out(multiplexer_3_out), .sel(control_alpha_1_branch));  // open: en
  ALU_16_bits alu_16_bits_1 (
    .a(registerfile_1_out_a), .b(multiplexer_2_out), .Result(alu_16_bits_1_result));  // open: Operation, Ainvert, Bnegate, Overflow, Zero
  RAM #(.addrWidth(16), .dataWidth(16), .bus("separate")) ram_1 (.data(ram_1_data));  // open: addr, din, str, sel, clk, ld, clr
  Multiplexer #(.width(16)) multiplexer_4 (.in0(ram_1_data), .out(multiplexer_4_out));  // open: in1, sel, en

  // Notes on the sheet:
  //   contents of rom_1 (hex, n*v repeats v):
  //   3809 2 8 6 17 3 9 4 7 401 1110 1402 1882 804 c09 3481 809 1c09 2100 c02 2404 1130 3100 1402 1982 804
  //   c09 3481 809 3811 1881 381e
endmodule

module ALU_CONTROL (
  input  ALUOP0,
  input  ALUOP1,
  input  ALUOP2,
  output [1:0] OPERATION,
  output BNEGATE,
  output AINVERT
);

  wire and_1_out, and_2_out, and_3_out, and_4_out, not_1_out, not_2_out, not_3_out, not_4_out;

  and and_1 (and_1_out, ALUOP1, ALUOP2);
  not not_1 (not_1_out, ALUOP1);
  not not_2 (not_2_out, ALUOP2);
  not not_3 (not_3_out, ALUOP2);
  not not_4 (not_4_out, ALUOP2);
  or or_1 (OPERATION[0], and_1_out, ALUOP0);
  and and_2 (and_2_out, not_1_out, ALUOP2);
  and and_3 (and_3_out, ALUOP1, not_2_out);
  and and_4 (and_4_out, ALUOP1, not_3_out);
  and and_5 (AINVERT, ALUOP1, not_4_out);
  or or_2 (OPERATION[1], and_2_out, and_3_out);
  or or_3 (BNEGATE, and_4_out, ALUOP0);
endmodule
